# Fritzing sketch clock (saved by Fritzing 1.0.1rc)
breadboards: 1

parts:
  Part1 = Arduino Uno (Rev3)
  S2 = Round Pushbutton
  S1 = Round Pushbutton
  S0 = Round Pushbutton
  7-Segment_4-Digit = SO16 [chip_label=7SEG package=SO]
  R4 = Resistor [tolerance=±1% power=0.25 resistance=220 package=THT]
  R5 = Resistor [tolerance=±1% power=0.25 resistance=220 package=THT]
  R6 = Resistor [tolerance=±1% power=0.25 resistance=220 package=THT]
  R7 = Resistor [tolerance=±1% power=0.25W resistance=220 package=THT]
  R8 = Resistor [tolerance=±1% power=0.25 resistance=220 package=THT]
  R9 = Resistor [tolerance=±1% power=0.25W resistance=220 package=THT]
  R10 = Resistor [tolerance=±1% power=0.25 resistance=220 package=THT]
  R11 = Resistor [tolerance=±1% power=0.25 resistance=220 package=THT]
  J1 = Piezo Speaker
  R12 = Resistor [tolerance=±1% power=0.25 resistance=220 package=THT]

nets:
  N1: Part1.A0, S0.leg0
  N2: Part1.A1, S1.leg0
  N3: Part1.A2, S2.leg0
  N4: Part1.A5/SCL, J1.pin2
  N5: Part1.D8, R7.Pin_0
  N6: Part1.D9_PWM, R5.Pin_0
  N7: Part1.D10_PWM/SS, R10.Pin_0
  N8: Part1.D11_PWM/MOSI, R8.Pin_0
  N9: Part1.D12/MISO, R6.Pin_0
  N10: Part1.D13/SCK, R4.Pin_0
  GND: Part1.GND, S2.leg1, S1.leg1, S0.leg1, R12.Pin_0
  N11: Part1.D2, 7-Segment_4-Digit.1, 7-Segment_4-Digit.2
  N12: Part1.D3_PWM, 7-Segment_4-Digit.3
  N13: Part1.D4, 7-Segment_4-Digit.4
  N14: Part1.D5_PWM, 7-Segment_4-Digit.5
  N15: Part1.D6_PWM, R11.Pin_0
  N16: Part1.D7, R9.Pin_0
  N17: 7-Segment_4-Digit.6, R11.Pin_1
  N18: 7-Segment_4-Digit.9, R9.Pin_1
  N19: 7-Segment_4-Digit.10, R7.Pin_1
  N20: 7-Segment_4-Digit.11, R5.Pin_1
  N21: 7-Segment_4-Digit.12, R10.Pin_1
  N22: 7-Segment_4-Digit.13, R8.Pin_1
  N23: 7-Segment_4-Digit.14, R6.Pin_1
  N24: 7-Segment_4-Digit.15, R4.Pin_1
  N25: J1.pin1, R12.Pin_1
